# Fritzing sketch ArduinoLEDButtonControl (saved by Fritzing 0.9.9b)
breadboards: 1

parts:
  Part1 = Arduino Uno (Rev3) - ICSP
  S3 = Pushbutton [package="[SMD]"]
  LED2 = LED - 3mm [color="Red (633nm)" current=0.030 package="3 mm [THT]"]
  R1 = Resistor [tolerance=±5% resistance=220 package="0402 [SMD]"]
  R2 = Resistor [tolerance=±5% resistance=10000 package="0402 [SMD]"]

nets:
  N1: Part1.D8, R1.Pin_1
  N2: Part1.GND, LED2.cathode, R2.Pin_0
  N3: Part1.D7, S3.Pin_3, S3.Pin_4, R2.Pin_1
  N4: Part1.5V, S3.Pin_1, S3.Pin_2
  N5: LED2.anode, R1.Pin_0
