# Fritzing sketch ArduinoLEDPotentiometerControl (saved by Fritzing 0.9.9b)
breadboards: 1

parts:
  R1 = Rotary Potentiometer (Small) [maximum_resistance=100kΩ package=THT]
  Part1 = Arduino Uno (Rev3) - ICSP
  R2 = Resistor [tolerance=±5% resistance=220 package="2010 [SMD]"]
  LED1 = LED - 3mm [color="Red (633nm)" current=0.030 package="3 mm [THT]"]

nets:
  N1: R1.leg1, Part1.5V
  N2: R1.wiper, Part1.A0
  N3: R1.leg2, Part1.GND, LED1.cathode
  N4: Part1.D6_PWM, R2.Pin_1
  N5: R2.Pin_0, LED1.anode
